// Logisim project gap.circ as structural Verilog: 4 circuits, main circuit main
module main (
  input  SLCT,
  input  RARI,
  input  PCO,
  input  CLR,
  input  CE,
  input  J
);

  wire clock_1_out, n16b_reg_1_out_20, n16b_reg_1_out_21, n16b_reg_1_out_22, n16b_reg_1_out_23,
       n16b_reg_1_out_24, n16b_reg_1_out_25, n16b_reg_1_out_26, n16b_reg_1_out_27, n16b_reg_1_out_28,
       n16b_reg_1_out_29, n16b_reg_1_out_30, n16b_reg_1_out_31, n16b_reg_1_out_32, n16b_reg_1_out_33,
       n16b_reg_1_out_34, n16b_reg_1_out_35;
  wire [4:0] m_c_s_1_j_2, transistor_1_out;
  wire [15:0] pc_1__0___lsb_2, transistor_2_out;

  Clock clock_1 (.out(clock_1_out));
  pc pc_1 (
    ._0___LSB(transistor_2_out[0]), ._1(transistor_2_out[1]), ._2(transistor_2_out[2]),
    ._3(transistor_2_out[3]), ._4(transistor_2_out[4]), ._5(transistor_2_out[5]), ._6(transistor_2_out[6]),
    ._7(transistor_2_out[7]), ._8(transistor_2_out[8]), ._9(transistor_2_out[9]), ._10(transistor_2_out[10]),
    ._11(transistor_2_out[11]), ._12(transistor_2_out[12]), ._13(transistor_2_out[13]),
    ._14(transistor_2_out[14]), ._15___msb(transistor_2_out[15]), ._0___LSB_2(pc_1__0___lsb_2[0]),
    ._1_2(pc_1__0___lsb_2[1]), ._2_2(pc_1__0___lsb_2[2]), ._3_2(pc_1__0___lsb_2[3]),
    ._4_2(pc_1__0___lsb_2[4]), ._5_2(pc_1__0___lsb_2[5]), ._6_2(pc_1__0___lsb_2[6]),
    ._7_2(pc_1__0___lsb_2[7]), ._8_2(pc_1__0___lsb_2[8]), ._9_2(pc_1__0___lsb_2[9]),
    ._10_2(pc_1__0___lsb_2[10]), ._11_2(pc_1__0___lsb_2[11]), ._12_2(pc_1__0___lsb_2[12]),
    ._13_2(pc_1__0___lsb_2[13]), ._14_2(pc_1__0___lsb_2[14]), ._15___msb_2(pc_1__0___lsb_2[15]),
    .J(transistor_1_out[0]), .CE(transistor_1_out[1]), .CLR(transistor_1_out[2]), .CLK(clock_1_out));
  Transistor #(.\type ("n"), .gate("br"), .width(5)) transistor_1 (
    .in(m_c_s_1_j_2), .out(transistor_1_out), .gate(SLCT));
  M_C_S m_c_s_1 (
    .J(J), .J_2(m_c_s_1_j_2[0]), .SEL(SLCT), .CE_2(m_c_s_1_j_2[1]), .CE(CE), .CLR_2(m_c_s_1_j_2[2]),
    .CLR(CLR), .PCO_2(m_c_s_1_j_2[3]), .PCO(PCO), .RARI_2(m_c_s_1_j_2[4]), .RARI(RARI));
  Transistor #(.\type ("n"), .width(16)) transistor_2 (
    .in(pc_1__0___lsb_2), .out(transistor_2_out), .gate(transistor_1_out[3]));
  _16b_reg u_16b_reg_1 (
    ._0___LSB(transistor_2_out[0]), ._1(transistor_2_out[1]), ._2(transistor_2_out[2]),
    ._3(transistor_2_out[3]), ._4(transistor_2_out[4]), ._5(transistor_2_out[5]), ._6(transistor_2_out[6]),
    ._7(transistor_2_out[7]), ._8(transistor_2_out[8]), ._9(transistor_2_out[9]), ._10(transistor_2_out[10]),
    ._11(transistor_2_out[11]), ._12(transistor_2_out[12]), ._13(transistor_2_out[13]),
    ._14(transistor_2_out[14]), ._15___MSB(transistor_2_out[15]), .CLR(transistor_1_out[2]),
    .I(transistor_1_out[4]), .CLK(clock_1_out), .out_20(n16b_reg_1_out_20), .out_21(n16b_reg_1_out_21),
    .out_22(n16b_reg_1_out_22), .out_23(n16b_reg_1_out_23), .out_24(n16b_reg_1_out_24),
    .out_25(n16b_reg_1_out_25), .out_26(n16b_reg_1_out_26), .out_27(n16b_reg_1_out_27),
    .out_28(n16b_reg_1_out_28), .out_29(n16b_reg_1_out_29), .out_30(n16b_reg_1_out_30),
    .out_31(n16b_reg_1_out_31), .out_32(n16b_reg_1_out_32), .out_33(n16b_reg_1_out_33),
    .out_34(n16b_reg_1_out_34), .out_35(n16b_reg_1_out_35));
endmodule

// PC
module pc (
  input  J,
  input  CE,
  input  CLR,
  input  CLK,
  input  _0___LSB,
  input  _1,
  input  _2,
  input  _3,
  input  _4,
  input  _5,
  input  _6,
  input  _7,
  input  _8,
  input  _9,
  input  _10,
  input  _11,
  input  _12,
  input  _13,
  input  _14,
  input  _15___msb,
  output _0___LSB_2,
  output _1_2,
  output _2_2,
  output _3_2,
  output _4_2,
  output _5_2,
  output _6_2,
  output _7_2,
  output _8_2,
  output _9_2,
  output _10_2,
  output _11_2,
  output _12_2,
  output _13_2,
  output _14_2,
  output _15___msb_2
);

  wire dip_74161_1_p7, dip_74161_2_p9, dip_74161_3_p9, not_1_out, not_2_out;

  not not_1 (not_1_out, J);
  not not_2 (not_2_out, CLR);
  // DIP_74161 dip_74161_1: pin names not known; wires that end beside it: not_2_out, CLK, _0___LSB, _1, _2, _3, dip_74161_1_p7, _0___LSB_2, _1_2, _2_2, _3_2
  // DIP_74161 dip_74161_2: pin names not known; wires that end beside it: not_2_out, dip_74161_1_p7, _4, _5, _6, _7, CE, not_1_out, dip_74161_2_p9, _4_2, _5_2, _6_2, _7_2
  // DIP_74161 dip_74161_3: pin names not known; wires that end beside it: not_2_out, dip_74161_2_p9, _8, _9, _10, _11, CE, not_1_out, dip_74161_3_p9, _8_2, _9_2, _10_2, _11_2
  // DIP_74161 dip_74161_4: pin names not known; wires that end beside it: not_2_out, dip_74161_3_p9, _12, _13, _14, _15___msb, CE, not_1_out, _12_2, _13_2, _14_2, _15___msb_2, CE, not_1_out
endmodule

module M_C_S (
  input  SEL,
  input  J,
  input  CE,
  input  CLR,
  input  PCO,
  input  RARI,
  output J_2,
  output CE_2,
  output CLR_2,
  output PCO_2,
  output RARI_2
);

  and and_1 (J_2, SEL, J);
  and and_2 (CE_2, SEL, CE);
  and and_3 (CLR_2, SEL, CLR);
  and and_4 (PCO_2, SEL, PCO);
  and and_5 (RARI_2, SEL, RARI);
endmodule

// RAR
module _16b_reg (
  input  CLR,
  input  I,
  input  CLK,
  input  _0___LSB,
  input  _1,
  input  _2,
  input  _3,
  input  _4,
  input  _5,
  input  _6,
  input  _7,
  input  _8,
  input  _9,
  input  _10,
  input  _11,
  input  _12,
  input  _13,
  input  _14,
  input  _15___MSB,
  output out_20,
  output out_21,
  output out_22,
  output out_23,
  output out_24,
  output out_25,
  output out_26,
  output out_27,
  output out_28,
  output out_29,
  output out_30,
  output out_31,
  output out_32,
  output out_33,
  output out_34,
  output out_35
);

  wire not_1_out;

  not not_1 (not_1_out, I);
  // IC_74173 ic_74173_1: pin names not known; wires that end beside it: _0___LSB, _1, _2, _3, CLK, out_20, out_21, out_22, out_23
  // IC_74173 ic_74173_2: pin names not known; wires that end beside it: not_1_out, _4, _5, CLK, CLR, 1'b0, out_24, out_25, out_26, out_27
  // IC_74173 ic_74173_3: pin names not known; wires that end beside it: not_1_out, _8, _9, _10, _11, CLK, CLR, 1'b0, out_28, out_29, out_30, out_31
  // IC_74173 ic_74173_4: pin names not known; wires that end beside it: not_1_out, _12, _13, _14, _15___MSB, CLK, not_1_out, CLR, CLR, 1'b0, 1'b0, out_32, out_33, out_34, out_35

  assign _7 = _6;
endmodule
